// Logisim project bt3.1.circ as structural Verilog: 1 circuit, main circuit main
module main (
  input  in_1,
  input  in_2,
  input  in_3,
  input  in_4,
  input  in_5,
  output out_6,
  output out_7,
  output out_8
);

  wire and_1_out, and_2_out, and_3_out, and_4_out, nand_1_out, nor_1_out, not_1_out, not_2_out, not_3_out,
       not_4_out, xnor_1_out;

  not not_1 (not_1_out, in_2);
  not not_2 (not_2_out, in_1);
  not not_3 (not_3_out, in_1);
  not not_4 (not_4_out, in_2);
  and and_1 (and_1_out, in_1, in_1, not_1_out);
  and and_2 (and_2_out, not_2_out, in_2);
  and and_3 (and_3_out, not_3_out, not_4_out);
  and and_4 (and_4_out, in_1, in_2);
  nor nor_1 (nor_1_out, in_3, in_4);
  nand nand_1 (nand_1_out, in_3, in_5);
  xnor xnor_1 (xnor_1_out, in_4, in_5);
  or or_1 (out_6, and_1_out, and_2_out);
  or or_2 (out_7, and_3_out, and_4_out);
  ExactlyOne xor_1 (.out(out_8), .in0(nor_1_out), .in2(nand_1_out), .in4(xnor_1_out));
endmodule
