// Logisim project Lab2-3.3.circ as structural Verilog: 1 circuit, main circuit main
module main (
  input  in_1,
  input  [2:0] in_2,
  output [3:0] out_3
);

  wire and_1_out, and_2_out, and_3_out, and_4_out, and_5_out, and_6_out, and_7_out, and_8_out, not_1_out,
       not_2_out, not_3_out, not_4_out, not_5_out, not_6_out, not_7_out, not_8_out, not_9_out;

  not not_1 (not_1_out, in_2[0]);
  not not_2 (not_2_out, in_2[2]);
  not not_3 (not_3_out, in_2[1]);
  not not_4 (not_4_out, in_2[0]);
  not not_5 (not_5_out, in_2[2]);
  not not_6 (not_6_out, in_2[1]);
  not not_7 (not_7_out, in_2[2]);
  not not_8 (not_8_out, in_2[1]);
  not not_9 (not_9_out, in_2[0]);
  and and_1 (and_1_out, in_2[1], not_1_out);
  and and_2 (and_2_out, in_2[2], in_2[1]);
  and and_3 (and_3_out, not_2_out, not_3_out, not_4_out);
  and and_4 (and_4_out, not_5_out, in_2[1], in_2[0]);
  and and_5 (and_5_out, in_2[2], not_6_out, in_2[0]);
  and and_6 (and_6_out, not_7_out, not_8_out, in_2[0]);
  and and_7 (and_7_out, in_2[1], not_9_out);
  and and_8 (and_8_out, in_2[2], in_2[1]);
  or or_1 (out_3[2], and_1_out, and_2_out);
  or or_2 (out_3[1], and_3_out, and_4_out, and_5_out);
  or or_3 (out_3[0], and_6_out, and_7_out, and_8_out);
  Hex_Digit_Display hex_digit_display_1 (.value({in_1, out_3[2:0]}));  // open: dp

  assign out_3[3] = in_1;
endmodule
